# Fritzing sketch circuit (saved by Fritzing 0.9.1b)

parts:
  12V/5A_power_supply = Power plug
  Arduino = Arduino Uno (Rev3)
  12V_Relay = Keyes Relay [package=THT]
  5A_fuse = FUSE [package=fuse_5mm]
  5A_fuse_2 = FUSE [package=fuse_5mm]
  12V_Water_Pump = DC Motor
  LED1 = LED - 5mm [color="Red (633nm)" package="5 mm [THT]"]
  R1 = Resistor [tolerance=±5% resistance=220 package=THT]
  Signal_switch = SWITCH-SPST-2 [package=switch-spst-vertical]
  LED2 = LED - 5mm [color="Red (633nm)" package="5 mm [THT]"]
  R2 = Resistor [tolerance=±5% resistance=220 package=THT]
  R3 = Resistor [tolerance=±5% resistance=220 package=THT]
  LED3 = LED - 5mm [color="Red (633nm)" package="5 mm [THT]"]
  F1 = FUSE [package=fuse_5mm]

nets:
  GND: 12V/5A_power_supply.GND, Arduino.GND, 12V_Relay.ground, 5A_fuse_2.1, LED1.cathode, Signal_switch.P, LED2.cathode, LED3.cathode
  N1: 12V/5A_power_supply.VCC, 5A_fuse.1, F1.2
  N2: Arduino.D2, Signal_switch.O
  N3: Arduino.D3_PWM, 12V_Relay.signal
  N4: Arduino.D4, R1.Pin_0
  N5: Arduino.D5_PWM, R2.Pin_0
  N6: Arduino.D6_PWM, R3.Pin_0
  N7: Arduino.5V, 12V_Relay.power
  N8: Arduino.VIN, F1.1
  N9: 12V_Relay.C, 5A_fuse.2
  N10: 12V_Relay.NO, 12V_Water_Pump.pin_2
  N11: 5A_fuse_2.2, 12V_Water_Pump.pin_1
  N12: LED1.anode, R1.Pin_1
  N13: LED2.anode, R2.Pin_1
  N14: R3.Pin_1, LED3.anode

notes:
  a 12V water pump
  5A fuses
  12V/5A power supply
  0.5A fuse

custom parts:
  Keyes Relay: The Keyes 5V relay module is suitable for SCM development, home appliance control. It uses a 5V~12V TIL control signal which can control DC / AC signal.
